# Fritzing sketch Umidificatore_Smart (saved by Fritzing 0.9.10b)
breadboards: 2

parts:
  Squix1 = OLED 0.96" 128x64 I2C SSD1306
  M1 = seeed grove atomizer v1.0
  Part1 = KY-015 Temperature & Humidity Sensor Module [package="Breakout board"]
  Water_Level_Sensor1 = Water Level Sensor [package=board]
  RE1 = KY-040 Rotary encoder [package="Breakout board"]
  Part2 = KY-016 RGB Full Color LED Module [package="Breakout board"]
  MH-ET_LIVE_ESP32_DEVKIT2 = MH-ET LIVE ESP32 DEVKIT 38 pins

nets:
  VCC: Squix1.VCC, M1.VCC, Part1.Vin, RE1.Vcc, MH-ET_LIVE_ESP32_DEVKIT2.5V
  GND: Squix1.GND, M1.GND, Part1.-, Water_Level_Sensor1.GND, RE1.GND, Part2.-, MH-ET_LIVE_ESP32_DEVKIT2.GND#58
  N1: Squix1.SCL, MH-ET_LIVE_ESP32_DEVKIT2.IO22
  N2: Squix1.SCA, MH-ET_LIVE_ESP32_DEVKIT2.IO21
  N3: M1.EN, MH-ET_LIVE_ESP32_DEVKIT2.IO4
  N4: Part1.S, MH-ET_LIVE_ESP32_DEVKIT2.IO14
  N5: Water_Level_Sensor1.SIG, MH-ET_LIVE_ESP32_DEVKIT2.IO34
  N6: Water_Level_Sensor1.VCC, MH-ET_LIVE_ESP32_DEVKIT2.IO27
  N7: RE1.SW, MH-ET_LIVE_ESP32_DEVKIT2.IO26
  N8: RE1.DT, MH-ET_LIVE_ESP32_DEVKIT2.IO25
  N9: RE1.CLK, MH-ET_LIVE_ESP32_DEVKIT2.IO33
  N10: Part2.R, MH-ET_LIVE_ESP32_DEVKIT2.IO32

custom parts:
  seeed grove atomizer v1.0: Grove - Water Atomization is a perfect module for you to quickly DIY a humidifier with Arduino. You can also develop more advanced and interesting projects with digital scent technology and any other situations in which atomization required.
  KY-015 Temperature & Humidity Sensor Module: DH-11 temperature and humidity sensor in KEYES KY-015 module, provides a low-latency serial interface to measure humidity and temperature.
  Water Level Sensor: A water level sensor. This sensor operates at 3V to 5V. The Sig (signal) pin outputs an analogue signal that is in proportion to the amount of water in contact with the sensor.
  KY-040 Rotary encoder: KY-040 Rotary Encoder with switch on breakout borad from AZ Delivery
  KY-016 RGB Full Color LED Module: KY-016 Arduino full color 5mm RGB LED, different colors can be obtained by mixing the three primary colors.
  MH-ET LIVE ESP32 DEVKIT 38 pins: http://mh.nodebb.com/topic/2/mh-et-live-esp32-devkit
